// Logisim project Vending.circ as structural Verilog: 6 circuits, main circuit main
module main (
  input  Halt_Enable
);

  wire and_2_out, CLK, Correct, Dime, Done_Testing, Give_Dime, Give_Merch, Give_Nickel, Halt, Nickel,
       not_1_out, not_2_out, not_3_out, Quarter, Sol_Give_Dime, Sol_Give_Merch, Sol_Give_Nickel;
  wire [8:0] counter_1_q, TestNumber;

  Clock clock_1 (.out(CLK));
  not not_1 (not_1_out, Correct);
  and and_1 (Halt, Halt_Enable, not_1_out);
  Inputs inputs_1 (
    .Halt(Halt), .CLK(CLK), .Quarter(Quarter), .Dime(Dime), .Nickel(Nickel), .TestNumber(TestNumber),
    .Done_Testing(Done_Testing));
  // Probe on Quarter
  // Probe on Dime
  // Probe on Nickel
  Vending vending_1 (
    .Quarter(Quarter), .Dime(Dime), .Nickel(Nickel), .CLK(CLK), .Give_Merchandise(Give_Merch),
    .Give_Dime(Give_Dime), .Give_Nickel(Give_Nickel));
  // Probe on Correct
  // Probe on Give_Merch
  // Probe on Sol_Give_Merch
  // Probe on Give_Dime
  // Probe on Sol_Give_Dime
  // Probe on Give_Nickel
  // Probe on Sol_Give_Nickel
  not not_2 (not_2_out, Halt);
  Checker checker_1 (
    .Give_Merch(Give_Merch), .Give_Dime(Give_Dime), .Give_Nickel(Give_Nickel), .TestNumber(TestNumber),
    .Correct(Correct), .Sol_Give_Merch(Sol_Give_Merch), .Sol_Give_Dime(Sol_Give_Dime),
    .Sol_Give_Nickel(Sol_Give_Nickel));
  and and_2 (and_2_out, Correct, not_2_out, not_3_out);
  not not_3 (not_3_out, Done_Testing);
  // Probe on counter_1_q
  Counter #(.width(9), .max('h162), .ongoal("stay")) counter_1 (
    .count(and_2_out), .Q(counter_1_q), .clk(CLK));  // open: load, D, carry, clr

  // Notes on the sheet:
  //   Yifei Chen 915188460
  //   Max 354
endmodule

module Vending (
  input  Quarter,
  input  Dime,
  input  Nickel,
  input  CLK,
  output Give_Merchandise,
  output Give_Dime,
  output Give_Nickel
);

  wire [2:0] circuit1_1_cp, curstate;

  circuit1 circuit1_1 (
    .a(curstate[2]), .b(curstate[1]), .c(curstate[0]), .q(Quarter), .d(Dime), .n(Nickel),
    .ap(circuit1_1_cp[2]), .bp(circuit1_1_cp[1]), .cp(circuit1_1_cp[0]));
  Register #(.width(3)) register_1 (.D(circuit1_1_cp), .Q(curstate), .clk(CLK));  // open: en, clr
  out out_1 (
    .ap(curstate[2]), .bp(curstate[1]), .cp(curstate[0]), .q(Quarter), .d(Dime), .n(Nickel),
    .z0(Give_Merchandise), .z1(Give_Dime), .z2(Give_Nickel));

  // Other names for the same wires on the sheet: Quater = Quarter
endmodule

module Inputs (
  input  Halt,
  input  CLK,
  output Quarter,
  output Dime,
  output Nickel,
  output [8:0] TestNumber,
  output Done_Testing
);

  wire not_1_out;

  not not_1 (not_1_out, Halt);
  Counter #(.width(9), .max('h162), .ongoal("stay")) counter_1 (
    .count(not_1_out), .Q(TestNumber), .carry(Done_Testing), .clk(CLK));  // open: load, D, clr
  ROM #(.addrWidth(9), .dataWidth(3)) rom_1 (.addr(TestNumber), .data({Quarter, Dime, Nickel}));  // open: sel

  // Notes on the sheet:
  //   contents of rom_1 (hex, n*v repeats v):
  //   1 0 1 0 1 0 1 0 1 0 1 0 1 0 1 0 1 0 1 0 1 0 2 0 1 0 1 0 1 0 1 0 1 0 4 0 1 0 1 0 1 0 1 0 2 0 1 0 1 0
  //   1 0 1 0 4 0 1 0 1 0 1 0 1 0 2 0 1 0 1 0 1 0 2 0 2 0 1 0 1 0 1 0 2 0 4 0 1 0 1 0 1 0 4 0 1 0 1 0 1 0
  //   1 0 2 0 1 0 1 0 1 0 2 0 2 0 1 0 1 0 1 0 2 0 4 0 1 0 1 0 2 0 2 0 1 0 1 0 2 0 4 0 1 0 1 0 4 0 1 0 1 0
  //   1 0 1 0 2 0 1 0 1 0 1 0 2 0 2 0 1 0 1 0 1 0 2 0 4 0 1 0 1 0 2 0 2 0 1 0 1 0 2 0 4 0 1 0 1 0 2 0 2 0
  //   1 0 2 0 2 0 2 0 1 0 2 0 2 0 4 0 1 0 2 0 4 0 1 0 4 0 1 0 1 0 1 0 1 0 2 0 1 0 1 0 1 0 2 0 2 0 1 0 1 0
  //   1 0 2 0 4 0 1 0 1 0 2 0 2 0 1 0 1 0 2 0 4 0 1 0 1 0 2 0 2 0 1 0 2 0 2 0 2 0 1 0 2 0 2 0 4 0 1 0 2 0
  //   4 0 1 0 1 0 2 0 2 0 1 0 2 0 2 0 2 0 1 0 2 0 2 0 4 0 2 0 2 0 2 0 2 0 2 0 4 0 2 0 4 0 1 0 4 0 2 0 4 0
  //   4 0 4
endmodule

module Checker (
  input  Give_Merch,
  input  Give_Dime,
  input  Give_Nickel,
  input  [8:0] TestNumber,
  output Correct,
  output Sol_Give_Merch,
  output Sol_Give_Dime,
  output Sol_Give_Nickel
);

  ROM #(.addrWidth(9), .dataWidth(3)) rom_1 (
    .addr(TestNumber), .data({Sol_Give_Merch, Sol_Give_Dime, Sol_Give_Nickel}));  // open: sel
  Comparator #(.width(3)) comparator_1 (
    .a({Sol_Give_Merch, Sol_Give_Dime, Sol_Give_Nickel}), .b({Give_Merch, Give_Dime, Give_Nickel}),
    .eq(Correct));  // open: gt, lt

  // Other names for the same wires on the sheet: Solution[2:0] = {Sol_Give_Merch, Sol_Give_Dime, Sol_Give_Nickel};
  //   Your_Answer[2:0] = {Give_Merch, Give_Dime, Give_Nickel}

  // Notes on the sheet:
  //   contents of rom_1 (hex, n*v repeats v):
  //   10*0 4 11*0 5 11*0 7 9*0 4 9*0 7 9*0 4 9*0 5 9*0 7 7*0 6 9*0 4 9*0 5 9*0 7 7*0 4 7*0 7 5*0 5 9*0 4
  //   9*0 5 9*0 7 7*0 4 7*0 7 7*0 4 7*0 5 7*0 7 5*0 6 0 0 0 4 9*0 4 9*0 5 9*0 7 7*0 4 7*0 7 7*0 4 7*0 5
  //   7*0 7 5*0 6 7*0 4 7*0 5 7*0 7 5*0 4 5*0 7 0 0 0 5 0 0 0 4 0 0 0 5 0 0 0 7
endmodule

module out (
  input  ap,
  input  bp,
  input  cp,
  input  q,
  input  d,
  input  n,
  output z0,
  output z1,
  output z2
);

  wire and_1_out, and_2_out, and_3_out, and_4_out, and_5_out, and_6_out, and_7_out, and_8_out, and_9_out,
       not_1_out;

  and and_1 (and_1_out, n, ap, cp);
  and and_2 (and_2_out, d, ap);
  and and_3 (and_3_out, q, cp);
  and and_4 (and_4_out, q, bp);
  and and_5 (and_5_out, q, bp, cp);
  and and_6 (and_6_out, q, ap);
  not not_1 (not_1_out, cp);
  or or_1 (z0, and_1_out, and_2_out, and_3_out, and_4_out);
  or or_2 (z1, and_5_out, and_6_out);
  and and_7 (and_7_out, bp, not_1_out, q);
  and and_8 (and_8_out, ap, q);
  and and_9 (and_9_out, ap, cp, d);
  or or_3 (z2, and_7_out, and_8_out, and_9_out);
endmodule

module circuit1 (
  input  a,
  input  b,
  input  c,
  input  q,
  input  d,
  input  n,
  output ap,
  output bp,
  output cp
);

  wire and_1_out, and_2_out, and_3_out, and_4_out, and_5_out, and_6_out, and_7_out, and_8_out, and_9_out,
       and_10_out, and_11_out, and_12_out, and_13_out, and_14_out, and_15_out, not_1_out, not_2_out,
       not_3_out, not_4_out, not_5_out, not_6_out, not_7_out, not_8_out, not_9_out, not_10_out, not_11_out,
       not_12_out, not_13_out, not_14_out, not_15_out, not_16_out, not_17_out, not_18_out, not_19_out,
       not_20_out, not_21_out, not_22_out, not_23_out, not_24_out, not_25_out, not_26_out, not_27_out,
       not_28_out, not_29_out, not_30_out, not_31_out;

  not not_1 (not_1_out, b);
  not not_2 (not_2_out, c);
  not not_3 (not_3_out, a);
  not not_4 (not_4_out, a);
  not not_5 (not_5_out, c);
  not not_6 (not_6_out, q);
  not not_7 (not_7_out, d);
  not not_8 (not_8_out, q);
  not not_9 (not_9_out, d);
  not not_10 (not_10_out, n);
  not not_11 (not_11_out, b);
  not not_12 (not_12_out, b);
  not not_13 (not_13_out, c);
  not not_14 (not_14_out, b);
  not not_15 (not_15_out, a);
  not not_16 (not_16_out, q);
  not not_17 (not_17_out, c);
  not not_18 (not_18_out, q);
  not not_19 (not_19_out, d);
  not not_20 (not_20_out, q);
  not not_21 (not_21_out, d);
  not not_22 (not_22_out, n);
  not not_23 (not_23_out, c);
  not not_24 (not_24_out, b);
  not not_25 (not_25_out, c);
  not not_26 (not_26_out, a);
  not not_27 (not_27_out, q);
  not not_28 (not_28_out, n);
  not not_29 (not_29_out, q);
  not not_30 (not_30_out, d);
  not not_31 (not_31_out, n);
  and and_1 (and_1_out, not_1_out, not_2_out, q);
  and and_2 (and_2_out, not_3_out, b, d);
  and and_3 (and_3_out, not_4_out, b, c, n);
  and and_4 (and_4_out, a, not_5_out, not_6_out, not_7_out);
  and and_5 (and_5_out, a, not_8_out, not_9_out, not_10_out);
  and and_6 (and_6_out, not_11_out, d);
  and and_7 (and_7_out, not_12_out, not_13_out, q);
  and and_8 (and_8_out, not_14_out, c, n);
  and and_9 (and_9_out, not_15_out, b, not_16_out);
  and and_10 (and_10_out, a, not_17_out, not_18_out, not_19_out);
  and and_11 (and_11_out, a, not_20_out, not_21_out, not_22_out);
  and and_12 (and_12_out, not_23_out, n);
  and and_13 (and_13_out, not_24_out, not_25_out, q);
  and and_14 (and_14_out, not_26_out, c, not_27_out, not_28_out);
  and and_15 (and_15_out, c, not_29_out, not_30_out, not_31_out);
  or or_1 (ap, and_1_out, and_2_out, and_3_out, and_4_out, and_5_out);
  or or_2 (bp, and_6_out, and_7_out, and_8_out, and_9_out, and_10_out, and_11_out);
  or or_3 (cp, and_12_out, and_13_out, and_14_out, and_15_out);
endmodule
