// Logisim project CPU.circ as structural Verilog: 4 circuits, main circuit Reg_File
module CPU (
);

  wire CLK, halt, multiplexer_1_out, nop, Reg_Write, Rtype;
  wire [3:0] A, A_Data, B_Data, B_I, C, multiplexer_2_out, opcode, Result;
  wire [4:0] counter_1_q;

  Clock clock_1 (.out(CLK));
  // Probe on counter_1_q
  Counter #(.width(5), .max('h1f)) counter_1 (
    .Q(counter_1_q), .clk(multiplexer_1_out));  // open: load, D, count, carry, clr
  Multiplexer #(.enable("false")) multiplexer_1 (.in0(CLK), .in1(1'b0), .out(multiplexer_1_out), .sel(halt));
  decoder decoder_1 (
    .bit0(opcode[3]), .bit1(opcode[2]), .bit2(opcode[1]), .bit3(opcode[0]), .halt(halt), .nop(nop), .R(Rtype));
  ROM #(.addrWidth(5), .dataWidth(16)) rom_1 (.addr(counter_1_q), .data({opcode, C, A, B_I}));  // open: sel
  // Probe on opcode
  // Probe on B_I
  Multiplexer #(.width(4), .enable("false")) multiplexer_2 (
    .in0(B_I), .in1(B_Data), .out(multiplexer_2_out), .sel(Rtype));
  // Probe on opcode
  // Probe on multiplexer_2_out
  // Probe on Result
  ALU alu_1 (.A(A_Data), .B(multiplexer_2_out), .opcode(opcode), .Result(Result));
  // Probe on B_Data
  // Probe on A_Data
  Reg_File reg_file_1 (
    .A(A), .B(B_I), .C(C), .Data_In(Result), .Reg_Write(Reg_Write), .CLK(CLK), .A_DATA(A_Data),
    .B_DATA(B_Data));
  nor nor_1 (Reg_Write, nop, halt);

  // Notes on the sheet:
  //   Instructions
  //   contents of rom_1 (hex, n*v repeats v):
  //   2003 2106 1005 3210 4301 5433 6520 763c 8720 986f b938 ca77 db13 ec62 fd85 e05
endmodule

module Reg_File (
  input  [3:0] A,
  input  [3:0] B,
  input  [3:0] C,
  input  [3:0] Data_In,
  input  Reg_Write,
  input  CLK,
  output [3:0] A_DATA,
  output [3:0] B_DATA
);

  wire Write_Reg0, Write_Reg1, Write_Reg2, Write_Reg3, Write_Reg4, Write_Reg5, Write_Reg6, Write_Reg7,
       Write_Reg8, Write_Reg9, Write_Reg10, Write_Reg11, Write_Reg12, Write_Reg13, Write_Reg14, Write_Reg15;
  wire [3:0] Reg0, Reg1, Reg2, Reg3, Reg4, Reg5, Reg6, Reg7, Reg8, Reg9, Reg10, Reg11, Reg12, Reg13, Reg14,
       Reg15;

  Demultiplexer #(.select(4), .enable("false")) demultiplexer_1 (
    .out0(Write_Reg0), .out1(Write_Reg1), .out2(Write_Reg2), .out3(Write_Reg3), .out4(Write_Reg4),
    .out5(Write_Reg5), .out6(Write_Reg6), .out7(Write_Reg7), .out8(Write_Reg8), .out9(Write_Reg9),
    .out10(Write_Reg10), .out11(Write_Reg11), .out12(Write_Reg12), .out13(Write_Reg13), .out14(Write_Reg14),
    .out15(Write_Reg15), .in(Reg_Write), .sel(C));
  // Probe on Reg0
  Register #(.width(4)) u_Reg0 (.D(Data_In), .en(Write_Reg0), .Q(Reg0), .clk(CLK));  // open: clr
  // Probe on Reg4
  Register #(.width(4)) u_Reg4 (.D(Data_In), .en(Write_Reg4), .Q(Reg4), .clk(CLK));  // open: clr
  // Probe on Reg8
  Register #(.width(4)) u_Reg8 (.D(Data_In), .en(Write_Reg8), .Q(Reg8), .clk(CLK));  // open: clr
  // Probe on Reg12
  Register #(.width(4)) u_Reg12 (.D(Data_In), .en(Write_Reg12), .Q(Reg12), .clk(CLK));  // open: clr
  // Probe on Reg1
  Register #(.width(4)) u_Reg1 (.D(Data_In), .en(Write_Reg1), .Q(Reg1), .clk(CLK));  // open: clr
  // Probe on Reg5
  Register #(.width(4)) u_Reg5 (.D(Data_In), .en(Write_Reg5), .Q(Reg5), .clk(CLK));  // open: clr
  // Probe on Reg9
  Register #(.width(4)) u_Reg9 (.D(Data_In), .en(Write_Reg9), .Q(Reg9), .clk(CLK));  // open: clr
  // Probe on Reg13
  Register #(.width(4)) u_Reg13 (.D(Data_In), .en(Write_Reg13), .Q(Reg13), .clk(CLK));  // open: clr
  Register #(.width(4)) u_Reg2 (.D(Data_In), .en(Write_Reg2), .Q(Reg2), .clk(CLK));  // open: clr
  Register #(.width(4)) u_Reg6 (.D(Data_In), .en(Write_Reg6), .Q(Reg6), .clk(CLK));  // open: clr
  Register #(.width(4)) u_Reg10 (.D(Data_In), .en(Write_Reg10), .Q(Reg10), .clk(CLK));  // open: clr
  Register #(.width(4)) u_Reg14 (.D(Data_In), .en(Write_Reg14), .Q(Reg14), .clk(CLK));  // open: clr
  // Probe on Reg2
  // Probe on Reg6
  // Probe on Reg10
  // Probe on Reg14
  // Probe on Reg3
  Register #(.width(4)) u_Reg3 (.D(Data_In), .en(Write_Reg3), .Q(Reg3), .clk(CLK));  // open: clr
  // Probe on Reg7
  Register #(.width(4)) u_Reg7 (.D(Data_In), .en(Write_Reg7), .Q(Reg7), .clk(CLK));  // open: clr
  // Probe on Reg11
  Register #(.width(4)) u_Reg11 (.D(Data_In), .en(Write_Reg11), .Q(Reg11), .clk(CLK));  // open: clr
  // Probe on Reg15
  Register #(.width(4)) u_Reg15 (.D(Data_In), .en(Write_Reg15), .Q(Reg15), .clk(CLK));  // open: clr
  Multiplexer #(.select(4), .width(4), .enable("false")) multiplexer_1 (
    .in0(Reg0), .in1(Reg1), .in2(Reg2), .in3(Reg3), .in4(Reg4), .in5(Reg5), .in6(Reg6), .in7(Reg7),
    .in8(Reg8), .in9(Reg9), .in10(Reg10), .in11(Reg11), .in12(Reg12), .in13(Reg13), .in14(Reg14),
    .in15(Reg15), .out(A_DATA), .sel(A));
  Multiplexer #(.select(4), .width(4), .enable("false")) multiplexer_2 (
    .in0(Reg0), .in1(Reg1), .in2(Reg2), .in3(Reg3), .in4(Reg4), .in5(Reg5), .in6(Reg6), .in7(Reg7),
    .in8(Reg8), .in9(Reg9), .in10(Reg10), .in11(Reg11), .in12(Reg12), .in13(Reg13), .in14(Reg14),
    .in15(Reg15), .out(B_DATA), .sel(B));
endmodule

module ALU (
  input  [3:0] A,
  input  [3:0] B,
  input  [3:0] opcode,
  output [3:0] Result
);

  wire [3:0] ADDR_ADDI, ANDR_ANDI, NEGATE, NOT, ORR_ORI, SUBR_SUBI, XORR_XORI;

  assign ANDR_ANDI = A & B;  // AND_Gate and_1, 4 bits wide
  assign ORR_ORI = A | B;  // OR_Gate or_1, 4 bits wide
  assign XORR_XORI = A ^ B;  // XOR_Gate xor_1, 4 bits wide
  assign NOT = ~A;  // NOT_Gate not_1, 4 bits wide
  Negator #(.width(4)) negator_1 (.in(A), .out(NEGATE));
  Adder #(.width(4)) adder_1 (.a(A), .b(B), .out(ADDR_ADDI));  // open: cin, cout
  Subtractor #(.width(4)) subtractor_1 (.a(A), .b(B), .out(SUBR_SUBI));  // open: bin, bout
  Multiplexer #(.select(4), .width(4), .enable("false")) multiplexer_1 (
    .in0(4'b0000), .in1(4'b0000), .in2(B), .in3(A), .in4(ANDR_ANDI), .in5(ANDR_ANDI), .in6(ORR_ORI),
    .in7(ORR_ORI), .in8(XORR_XORI), .in9(XORR_XORI), .in10(NOT), .in11(NEGATE), .in12(ADDR_ADDI),
    .in13(ADDR_ADDI), .in14(SUBR_SUBI), .in15(SUBR_SUBI), .out(Result), .sel(opcode));
endmodule

module decoder (
  input  bit0,
  input  bit1,
  input  bit2,
  input  bit3,
  output halt,
  output nop,
  output R
);

  wire and_1_out, and_2_out, and_3_out, not_1_out, not_2_out, not_3_out, not_4_out, not_5_out, not_6_out,
       not_7_out, not_8_out, not_9_out, not_10_out;

  not not_1 (not_1_out, bit0);
  not not_2 (not_2_out, bit1);
  not not_3 (not_3_out, bit2);
  not not_4 (not_4_out, bit3);
  not not_5 (not_5_out, bit0);
  not not_6 (not_6_out, bit1);
  not not_7 (not_7_out, bit2);
  not not_8 (not_8_out, bit1);
  and and_1 (and_1_out, not_8_out, bit2, bit3);
  and and_2 (and_2_out, bit1, not_9_out);
  not not_9 (not_9_out, bit3);
  and and_3 (and_3_out, bit0, not_10_out);
  not not_10 (not_10_out, bit3);
  and and_4 (halt, not_1_out, not_2_out, not_3_out, not_4_out);
  and and_5 (nop, not_5_out, not_6_out, not_7_out, bit3);
  or or_1 (R, and_1_out, and_2_out, and_3_out);
endmodule
