// Logisim project Cache.circ as structural Verilog: 9 circuits, main circuit main
module main (
  input  EnableTestHalting,
  output [9:0] CorrectCounter,
  output [9:0] HitCounter,
  output [9:0] MissCounter,
  output [9:0] TestNumber,
  output [7:0] ByteRead,
  output [7:0] CorrectByteRead,
  output Halt
);

  wire and_3_out, and_4_out, and_5_out, CLK, CmdIsRead, Correct, CpuRead, CpuWrite, DidContain, HaltTesting,
       MaxItersReached, MemRead, MemWrite, not_1_out, not_2_out, not_4_out, NotDoneTesting, Ok2Count,
       or_1_out, Ready;
  wire [7:0] CpuWriteValue, MemAddress;
  wire [9:0] CpuAddress;
  wire [31:0] Line2Mem, LineFromMem;

  not not_1 (not_1_out, Ready);
  Clock clock_1 (.out(CLK));
  or or_1 (or_1_out, MaxItersReached, Ready);
  Counter #(.width(4), .max('h9)) MaxClocks (
    .load(Ready), .D(4'b0001), .count(not_1_out), .carry(MaxItersReached), .clk(CLK));  // open: Q, clr
  and and_1 (HaltTesting, EnableTestHalting, CmdIsRead, not_2_out);
  not not_2 (not_2_out, Correct);
  not not_3 (NotDoneTesting, Halt);
  Inputs inputs_1 (
    .HaltTesting(HaltTesting), .Ready(or_1_out), .CLK(CLK), .Done(Halt), .Read(CpuRead), .Write(CpuWrite),
    .Address(CpuAddress), .Value(CpuWriteValue), .TestNumber(TestNumber));
  Cache cache_1 (
    .CpuAddress(CpuAddress), .CpuRead(CpuRead), .CpuWrite(CpuWrite), .CpuWriteValue(CpuWriteValue),
    .CLK(CLK), .Ready(Ready), .DidContain(DidContain), .ByteRead(ByteRead), .MemAddress(MemAddress),
    .MemRead(MemRead), .MemWrite(MemWrite), .LineFromMem(LineFromMem), .Line2Mem(Line2Mem));
  // Probe on CpuRead
  // Probe on CpuWrite
  // Probe on CpuAddress
  // Probe on CpuWriteValue
  // Probe on TestNumber
  // Probe on CorrectByteRead
  // Probe on Correct
  // Probe on Ready
  // Probe on DidContain
  // Probe on ByteRead
  // Probe on MemAddress
  // Probe on MemRead
  // Probe on MemWrite
  // Probe on HitCounter
  // Probe on LineFromMem
  // Probe on Line2Mem
  not not_4 (not_4_out, HaltTesting);
  RAM #(.dataWidth(32), .bus("separate")) ram_1 (
    .addr(MemAddress), .din(Line2Mem), .data(LineFromMem), .str(MemWrite), .clk(CLK), .ld(MemRead));  // open: sel, clr
  and and_2 (Ok2Count, Ready, not_4_out, NotDoneTesting);
  and and_3 (and_3_out, Correct, Ok2Count);
  and and_4 (and_4_out, DidContain, Ok2Count);
  and and_5 (and_5_out, MemRead, NotDoneTesting);
  Checker checker_1 (
    .TestNumber(TestNumber), .YourByteRead(ByteRead), .CmdIsRead(CmdIsRead),
    .CorrectByteRead(CorrectByteRead), .Correct(Correct));
  Counter #(.width(10), .max('h3ff)) u_CorrectCounter (
    .count(and_3_out), .Q(CorrectCounter), .clk(CLK));  // open: load, D, carry, clr
  Counter #(.width(10), .max('h3ff)) u_HitCounter (
    .count(and_4_out), .Q(HitCounter), .clk(CLK));  // open: load, D, carry, clr
  Counter #(.width(10), .max('h3ff)) u_MissCounter (
    .count(and_5_out), .Q(MissCounter), .clk(CLK));  // open: load, D, carry, clr
  // Probe on CorrectCounter
  // Probe on HitCounter
  // Probe on MissCounter

  // Other names for the same wires on the sheet: DoneTesting = Halt

  // Notes on the sheet:
  //   Your Answer Inside Here
endmodule

module Cache (
  input  [9:0] CpuAddress,
  input  CpuRead,
  input  CpuWrite,
  input  [7:0] CpuWriteValue,
  input  CLK,
  input  [31:0] LineFromMem,
  output Ready,
  output DidContain,
  output [7:0] ByteRead,
  output [7:0] MemAddress,
  output MemRead,
  output MemWrite,
  output [31:0] Line2Mem
);

  wire age, age0, age1, DidContain0, DidContain1, dirty0, dirty1, has, init, inputRead, inputWrite, isDirty,
       multiplexer_6_out, multiplexer_7_out, or_1_out, read0, read1, readySave, save, setDirty, toD0, toD1,
       valid, valid0, valid1, write0, write1, writeMode;
  wire [6:0] Tag0, Tag1;
  wire [7:0] val0, val1, WriteValue;
  wire [7:1] MemAddressWrite;
  wire [9:0] Address;
  wire [31:0] writer0, writer1;

  Register #(.width(1)) State (.D(CpuRead), .en(readySave), .Q(inputRead), .clk(CLK));  // open: clr
  Register #(.width(1)) State_2 (.D(CpuWrite), .en(readySave), .Q(inputWrite), .clk(CLK));  // open: clr
  Register State_3 (.D(CpuWriteValue), .en(readySave), .Q(WriteValue), .clk(CLK));  // open: clr
  Register #(.width(10)) State_4 (.D(CpuAddress), .en(readySave), .Q(Address), .clk(CLK));  // open: clr
  // Probe on Address
  Demultiplexer #(.enable("false")) demultiplexer_1 (.out0(valid0), .out1(valid1), .in(valid), .sel(Address[2]));
  Demultiplexer #(.enable("false")) demultiplexer_2 (.out0(age0), .out1(age1), .in(age), .sel(Address[2]));
  or or_1 (or_1_out, CpuRead, CpuWrite);
  // Probe on Address[9:3]
  and and_1 (readySave, or_1_out, Ready);
  Set Set0 (
    .Tag(Address[9:3]), .offset(Address[1:0]), .CLK(CLK), .valid(valid0), .age(age0), .dirty(toD0),
    .init(init), .read(read0), .write(write0), .requested_vals(LineFromMem), .write_singe_block(WriteValue),
    .DidContain(DidContain0), .toDirty(dirty0), .line2memo(writer0), .tag2write(Tag0), .readVal(val0));
  Multiplexer #(.enable("false")) multiplexer_1 (.in0(DidContain0), .in1(DidContain1), .out(has), .sel(Address[2]));
  Demultiplexer #(.enable("false")) demultiplexer_3 (.out0(read0), .out1(read1), .in(MemRead), .sel(Address[2]));
  Demultiplexer #(.enable("false")) demultiplexer_4 (.out0(toD0), .out1(toD1), .in(setDirty), .sel(Address[2]));
  Register #(.width(1)) State_5 (.D(has), .en(save), .Q(DidContain), .clk(CLK));  // open: clr
  Multiplexer #(.enable("false")) multiplexer_2 (.in0(dirty0), .in1(dirty1), .out(isDirty), .sel(Address[2]));
  Demultiplexer #(.enable("false")) demultiplexer_5 (.out0(write0), .out1(write1), .in(writeMode), .sel(Address[2]));
  // Probe on Address[9:3]
  Set Set1 (
    .Tag(Address[9:3]), .offset(Address[1:0]), .CLK(CLK), .valid(valid1), .age(age1), .dirty(toD1),
    .init(init), .read(read1), .write(write1), .requested_vals(LineFromMem), .write_singe_block(WriteValue),
    .DidContain(DidContain1), .toDirty(dirty1), .line2memo(writer1), .tag2write(Tag1), .readVal(val1));
  Multiplexer #(.width(32), .enable("false")) multiplexer_3 (
    .in0(writer0), .in1(writer1), .out(Line2Mem), .sel(Address[2]));
  Multiplexer #(.width(8), .enable("false")) multiplexer_4 (.in0(val0), .in1(val1), .out(ByteRead), .sel(Address[2]));
  Multiplexer #(.width(7), .enable("false")) multiplexer_5 (
    .in0(Tag0), .in1(Tag1), .out(MemAddressWrite), .sel(Address[2]));
  Multiplexer #(.enable("false")) multiplexer_6 (.in0(inputRead), .in1(CpuRead), .out(multiplexer_6_out), .sel(Ready));
  Multiplexer #(.enable("false")) multiplexer_7 (
    .in0(inputWrite), .in1(CpuWrite), .out(multiplexer_7_out), .sel(Ready));
  States states_1 (
    .read(multiplexer_6_out), .write(multiplexer_7_out), .contains(has), .dirty(isDirty), .CLK(CLK),
    .ready(Ready), .setDirty(setDirty), .valid(valid), .UpdateAge(age), .memRead(MemRead),
    .memWrite(MemWrite), .Write_2(writeMode), .init(init), .saveContain(save));
  // Probe on {MemAddressWrite, Address[2]}
  // Probe on Address[9:2]
  Multiplexer #(.width(8), .enable("false")) multiplexer_8 (
    .in0({MemAddressWrite, Address[2]}), .in1(Address[9:2]), .out(MemAddress), .sel(MemRead));

  // Other names for the same wires on the sheet: offset[1:0] = Address[1:0]; MemAddressRead[7:0] = Address[9:2];
  //   Tag[6:0] = Address[9:3]; MemAddressWrite[0] = Address[2]; Set = Address[2]

  // Notes on the sheet:
  //   Address Bits = 10
  //   Line Size = 4
  //   W = 3
  //   Num Sets = 2
  //   C =4*3*2 = 24bytes
  //   Tag bits = 7
endmodule

module Inputs (
  input  HaltTesting,
  input  Ready,
  input  CLK,
  output Done,
  output Read,
  output Write,
  output [9:0] Address,
  output [7:0] Value,
  output [9:0] TestNumber
);

  wire and_1_out, not_1_out, not_2_out;

  not not_1 (not_1_out, HaltTesting);
  not not_2 (not_2_out, Done);
  Counter #(.width(10), .max('h3ff), .ongoal("stay")) u_TestNumber (
    .count(and_1_out), .Q(TestNumber), .clk(CLK));  // open: load, D, carry, clr
  and and_1 (and_1_out, not_1_out, Ready, not_2_out);
  ROM #(.addrWidth(10), .dataWidth(21)) rom_1 (
    .addr(TestNumber), .data({Done, Read, Write, Address, Value}));  // open: sel

  // Notes on the sheet:
  //   contents of rom_1 (hex, n*v repeats v):
  //   80882 83fe6 4306b 83e0e 43701 42275 8280f 80304 41bd8 84371 43f77 41d70 4250b 44733 8253d 440d8
  //   82691 440c9 83d7c 43558 446bf 83837 842c9 43e0f 4059d 41556 80166 833b0 43a89 83142 8361c 42e66
  //   43eb6 42c00 43a0e 8165c 84682 8092a 83907 41f89 817b0 40855 82056 425e8 43ff2 8039f 42bd7 82137
  //   4416b 40273 8324a 814e4 44570 41c0f 429da 82640 8069c 8099e 414d5 41004 81beb 84113 419b1 81add
  //   83f35 425ff 829cd 40250 82945 4366d 40cc2 444f8 80814 81156 8446d 42a82 42bae 82578 41135 405d0
  //   8304b 82b3a 40972 822ba 4443a 42337 82506 80bd3 80560 83552 83955 81434 43096 43da1 81aa2 80305
  //   428e6 428cc 808a2 40e80 845f0 4215d 82765 82e29 40be5 82b74 42715 417a2 41fab 8452f 81c0a 83325
  //   44624 80205 42dfc 41333 40958 81348 42736 41069 84510 44669 826dd 8067e 408e4 44680 444e8 832ad
  //   821f8 83509 82d46 81184 432cd 80b77 4005a 440e0 81ea0 43d73 42b8c 80624 41468 42699 415ed 80fc1 0
  //   100000
endmodule

module Checker (
  input  [9:0] TestNumber,
  input  [7:0] YourByteRead,
  output CmdIsRead,
  output [7:0] CorrectByteRead,
  output Correct
);

  wire comparator_1_eq;
  wire [9:0] subtractor_1_out;

  // Probe on TestNumber
  Subtractor #(.width(10)) subtractor_1 (.a(TestNumber), .b(10'h1), .out(subtractor_1_out));  // open: bin, bout
  ROM #(.addrWidth(10), .dataWidth(9)) rom_1 (
    .addr(subtractor_1_out), .data({CmdIsRead, CorrectByteRead}));  // open: sel
  Comparator #(.mode("unsigned")) comparator_1 (
    .a(YourByteRead), .b(CorrectByteRead), .eq(comparator_1_eq));  // open: gt, lt
  and and_1 (Correct, comparator_1_eq, CmdIsRead);

  // Other names for the same wires on the sheet: Test_Number[9:0] = TestNumber

  // Notes on the sheet:
  //   Read Solutions
  //   contents of rom_1 (hex, n*v repeats v):
  //   1a3 1dc 6b 125 1 75 1dc 1c3 d8 1ab 77 70 b 33 10b d8 1c3 c9 174 58 bf 153 199 f 9d 56 1bb 13b 89 16c
  //   180 66 b6 0 e 107 1bf 1d8 167 89 118 55 1a2 e8 f2 1c3 d7 142 6b 73 1ab 18c 70 f da 1c3 14c 1d8 d5 4
  //   1d8 16b b1 1f4 1f2 ff 1da 50 1da 6d c2 f8 155 1c6 1f8 82 ae 1ff 35 d0 16b 1ae 72 175 3a 37 1ff 173
  //   1d0 158 167 1d5 96 a1 1f4 1c3 e6 cc 155 80 170 5d 1e6 166 e5 1ae 15 a2 ab 170 10f 13b 24 150 fc 33
  //   58 133 36 69 170 69 1c3 14c e4 80 e8 1ab 15d 158 1fc 135 cd 1e5 5a e0 104 73 8c 14c 68 99 ed 1a6
endmodule

module Set (
  input  [6:0] Tag,
  input  [1:0] offset,
  input  CLK,
  input  valid,
  input  age,
  input  dirty,
  input  init,
  input  read,
  input  write,
  input  [31:0] requested_vals,
  input  [7:0] write_singe_block,
  output DidContain,
  output toDirty,
  output [31:0] line2memo,
  output [6:0] tag2write,
  output [7:0] readVal
);

  wire dirty0, dirty1, dirty2, shouldRead0, shouldRead1, shouldRead2, shouldWrite0, shouldWrite1,
       shouldWrite2, updateDirty0, updateDirty1, updateDirty2, updateValid0, updateValid1, updateValid2,
       valid0, valid1, valid2;
  wire [1:0] age0, age1, age2, selectedAge, selectedBlcok;
  wire [6:0] tag0, tag1, tag2;
  wire [7:0] val0, val1, val2;
  wire [31:0] writer0, writer1, writer2;

  // Probe on age0
  // Probe on age1
  // Probe on age2
  // Probe on nothing
  Demultiplexer #(.select(2), .enable("false")) demultiplexer_1 (
    .out0(updateValid0), .out1(updateValid1), .out2(updateValid2), .in(valid), .sel(selectedBlcok));  // open: out3
  // Probe on selectedBlcok
  Demultiplexer #(.select(2), .enable("false")) demultiplexer_2 (
    .out0(updateDirty0), .out1(updateDirty1), .out2(updateDirty2), .in(dirty), .sel(selectedBlcok));  // open: out3
  Multiplexer #(.select(2), .enable("false")) multiplexer_1 (
    .in0(dirty0), .in1(dirty1), .in2(dirty2), .out(toDirty), .sel(selectedBlcok));  // open: in3
  Line block0 (
    .Tag(Tag), .offset(offset), .updateDirty(updateDirty0), .updateAge(age), .updateValid(updateValid0),
    .init(init), .selected_age(selectedAge), .read(shouldRead0), .write(shouldWrite0),
    .write_single_block(write_singe_block), .memory_from_cpu(requested_vals), .CLK(CLK), .wayID(2'b00),
    .\output (val0), .val2memo(writer0), .valid(valid0), .dirty(dirty0), .age(age0), .curr_tag(tag0));
  Demultiplexer #(.select(2), .enable("false")) demultiplexer_3 (
    .out0(shouldRead0), .out1(shouldRead1), .out2(shouldRead2), .in(read), .sel(selectedBlcok));  // open: out3
  Demultiplexer #(.select(2), .enable("false")) demultiplexer_4 (
    .out0(shouldWrite0), .out1(shouldWrite1), .out2(shouldWrite2), .in(write), .sel(selectedBlcok));  // open: out3
  Multiplexer #(.select(2), .width(2), .enable("false")) multiplexer_2 (
    .in0(age0), .in1(age1), .in2(age2), .out(selectedAge), .sel(selectedBlcok));  // open: in3
  Line block1 (
    .Tag(Tag), .offset(offset), .updateDirty(updateDirty1), .updateAge(age), .updateValid(updateValid1),
    .init(init), .selected_age(selectedAge), .read(shouldRead1), .write(shouldWrite1),
    .write_single_block(write_singe_block), .memory_from_cpu(requested_vals), .CLK(CLK), .wayID(2'b01),
    .\output (val1), .val2memo(writer1), .valid(valid1), .dirty(dirty1), .age(age1), .curr_tag(tag1));
  Line block2 (
    .Tag(Tag), .offset(offset), .updateDirty(updateDirty2), .updateAge(age), .updateValid(updateValid2),
    .init(init), .selected_age(selectedAge), .read(shouldRead2), .write(shouldWrite2),
    .write_single_block(write_singe_block), .memory_from_cpu(requested_vals), .CLK(CLK), .wayID(2'b10),
    .\output (val2), .val2memo(writer2), .valid(valid2), .dirty(dirty2), .age(age2), .curr_tag(tag2));
  Matcher matcher_1 (
    .Tag(Tag), .tag0(tag0), .tag1(tag1), .tag2(tag2), .valid0(valid0), .valid1(valid1), .valid2(valid2),
    .age0(age0), .age1(age1), .age2(age2), .contains(DidContain), .selectedBlcok(selectedBlcok));
  // Probe on DidContain
  // Probe on selectedBlcok
  Multiplexer #(.select(2), .width(32), .enable("false")) multiplexer_3 (
    .in0(writer0), .in1(writer1), .in2(writer2), .out(line2memo), .sel(selectedBlcok));  // open: in3
  Multiplexer #(.select(2), .width(7), .enable("false")) multiplexer_4 (
    .in0(tag0), .in1(tag1), .in2(tag2), .out(tag2write), .sel(selectedBlcok));  // open: in3
  Multiplexer #(.select(2), .width(8), .enable("false")) multiplexer_5 (
    .in0(val0), .in1(val1), .in2(val2), .out(readVal), .sel(selectedBlcok));  // open: in3

  // Other names for the same wires on the sheet: contains = DidContain; in_tag[6:0] = Tag
endmodule

module Line (
  input  [6:0] Tag,
  input  [1:0] offset,
  input  updateDirty,
  input  updateAge,
  input  updateValid,
  input  init,
  input  [1:0] selected_age,
  input  read,
  input  write,
  input  [7:0] write_single_block,
  input  [31:0] memory_from_cpu,
  input  CLK,
  input  [1:0] wayID,
  output [7:0] \output ,
  output [31:0] val2memo,
  output valid,
  output dirty,
  output [1:0] age,
  output [6:0] curr_tag
);

  wire or_1_out, or_2_out, or_3_out;
  wire [1:0] agecontroller_1_newage;
  wire [31:0] multiplexer_1_out, new_vals;

  Multiplexer #(.width(32), .enable("false")) multiplexer_1 (
    .in0(new_vals), .in1(memory_from_cpu), .out(multiplexer_1_out), .sel(read));
  Register #(.width(7)) u_curr_Tag (.D(Tag), .en(or_1_out), .Q(curr_tag), .clk(CLK));  // open: clr
  or or_1 (or_1_out, read, write);
  Register #(.width(32)) Blocks (.D(multiplexer_1_out), .en(or_2_out), .Q(val2memo), .clk(CLK));  // open: clr
  or or_2 (or_2_out, read, write);
  Register #(.width(1)) u_valid (.D(updateValid), .en(read), .Q(valid), .clk(CLK));  // open: clr
  Register #(.width(1)) u_dirty (.D(updateDirty), .en(write), .Q(dirty), .clk(CLK));  // open: clr
  // Probe on val2memo
  Multiplexer #(.select(2), .width(32), .enable("false")) multiplexer_2 (
    .in0({val2memo[31:8], write_single_block}), .in1({val2memo[31:16], write_single_block, val2memo[7:0]}),
    .in2({val2memo[31:24], write_single_block, val2memo[15:0]}), .in3({write_single_block, val2memo[23:0]}),
    .out(new_vals), .sel(offset));
  // Probe on new_vals
  AgeController agecontroller_1 (
    .selectAge(selected_age), .ID(wayID), .currAge(age), .init(init), .newAge(agecontroller_1_newage));
  Register #(.width(2)) u_age (.D(agecontroller_1_newage), .en(or_3_out), .Q(age), .clk(CLK));  // open: clr
  or or_3 (or_3_out, updateAge, init);
  // Probe on age
  Multiplexer #(.select(2), .width(8), .enable("false")) multiplexer_3 (
    .in0(val2memo[7:0]), .in1(val2memo[15:8]), .in2(val2memo[23:16]), .in3(val2memo[31:24]), .out(\output ),
    .sel(offset));

  // Other names for the same wires on the sheet: curr_vals[31:0] = val2memo; V0[7:0] = val2memo[7:0];
  //   V1[7:0] = val2memo[15:8]; V2[7:0] = val2memo[23:16]; V3[7:0] = val2memo[31:24]; in_tag[6:0] = Tag;
  //   memo_vals[31:0] = memory_from_cpu
endmodule

module AgeController (
  input  [1:0] selectAge,
  input  [1:0] ID,
  input  [1:0] currAge,
  input  init,
  output [1:0] newAge
);

  wire comparator_1_eq, comparator_1_lt;
  wire [1:0] adder_1_out, multiplexer_1_out, multiplexer_2_out;

  Comparator #(.width(2), .mode("unsigned")) comparator_1 (
    .a(selectAge), .b(currAge), .eq(comparator_1_eq), .lt(comparator_1_lt));  // open: gt
  Adder #(.width(2)) adder_1 (.a(currAge), .b(2'b01), .out(adder_1_out));  // open: cin, cout
  Multiplexer #(.width(2), .enable("false")) multiplexer_1 (
    .in0(currAge), .in1(adder_1_out), .out(multiplexer_1_out), .sel(comparator_1_lt));
  Multiplexer #(.width(2), .enable("false")) multiplexer_2 (
    .in0(multiplexer_1_out), .in1(2'b00), .out(multiplexer_2_out), .sel(comparator_1_eq));
  Multiplexer #(.width(2), .enable("false")) multiplexer_3 (
    .in0(multiplexer_2_out), .in1(ID), .out(newAge), .sel(init));
endmodule

module Matcher (
  input  [6:0] Tag,
  input  [6:0] tag0,
  input  [6:0] tag1,
  input  [6:0] tag2,
  input  valid0,
  input  valid1,
  input  valid2,
  input  [1:0] age0,
  input  [1:0] age1,
  input  [1:0] age2,
  output contains,
  output [1:0] selectedBlcok
);

  wire comparator_1_eq, comparator_2_eq, comparator_3_eq, comparator_4_lt, comparator_5_lt, comparator_6_lt,
       comparator_7_lt;
  wire [1:0] hit, local_max, local_max_ID, max_overwrite, to_overwrite;
  wire [2:0] and_1_out;

  Comparator #(.width(7), .mode("unsigned")) comparator_1 (.a(Tag), .b(tag0), .eq(comparator_1_eq));  // open: gt, lt
  Comparator #(.width(7), .mode("unsigned")) comparator_2 (.a(Tag), .b(tag1), .eq(comparator_2_eq));  // open: gt, lt
  Comparator #(.width(7), .mode("unsigned")) comparator_3 (.a(Tag), .b(tag2), .eq(comparator_3_eq));  // open: gt, lt
  Comparator #(.width(2), .mode("unsigned")) comparator_4 (.a(age0), .b(age1), .lt(comparator_4_lt));  // open: gt, eq
  Multiplexer #(.width(2), .enable("false")) multiplexer_1 (
    .in0(age0), .in1(age1), .out(local_max), .sel(comparator_4_lt));
  Comparator #(.width(2), .mode("unsigned")) comparator_5 (.a(age0), .b(age1), .lt(comparator_5_lt));  // open: gt, eq
  Multiplexer #(.width(2), .enable("false")) multiplexer_2 (
    .in0(2'b00), .in1(2'b01), .out(local_max_ID), .sel(comparator_5_lt));
  and and_1 (and_1_out[0], comparator_1_eq, valid0);
  and and_2 (and_1_out[1], comparator_2_eq, valid1);
  and and_3 (and_1_out[2], comparator_3_eq, valid2);
  // Probe on local_max
  // Probe on local_max_ID
  BitFinder #(.width(3)) bitfinder_1 (.in(and_1_out), .index(hit), .found(contains));
  Comparator #(.width(2), .mode("unsigned")) comparator_6 (
    .a(local_max), .b(age2), .lt(comparator_6_lt));  // open: gt, eq
  Multiplexer #(.width(2), .enable("false")) multiplexer_3 (
    .in0(local_max), .in1(age2), .out(max_overwrite), .sel(comparator_6_lt));
  // Probe on hit
  // Probe on max_overwrite
  Comparator #(.width(2), .mode("unsigned")) comparator_7 (
    .a(local_max), .b(age2), .lt(comparator_7_lt));  // open: gt, eq
  Multiplexer #(.width(2), .enable("false")) multiplexer_4 (
    .in0(local_max_ID), .in1(2'b10), .out(to_overwrite), .sel(comparator_7_lt));
  // Probe on to_overwrite
  Multiplexer #(.width(2), .enable("false")) multiplexer_5 (
    .in0(to_overwrite), .in1(hit), .out(selectedBlcok), .sel(contains));

  // Other names for the same wires on the sheet: in_tag[6:0] = Tag
endmodule

module States (
  input  read,
  input  write,
  input  contains,
  input  dirty,
  input  CLK,
  output ready,
  output setDirty,
  output valid,
  output UpdateAge,
  output memRead,
  output memWrite,
  output Write_2,
  output init,
  output saveContain
);

  wire and_1_out, and_2_out, and_3_out, and_4_out, and_5_out, and_6_out, and_7_out, and_8_out, and_9_out,
       and_10_out, and_11_out, and_12_out, and_13_out, and_14_out, not_1_out, not_2_out, not_3_out,
       not_4_out, not_5_out, not_6_out, not_7_out, not_8_out, not_9_out, not_10_out, not_11_out, not_12_out,
       not_13_out, not_14_out, not_15_out, not_16_out, not_17_out, not_18_out, not_19_out, not_20_out,
       not_21_out, not_22_out, not_23_out, not_24_out, not_25_out, not_26_out, not_27_out, not_28_out,
       not_29_out, not_30_out, not_31_out, not_32_out, or_1_out, or_2_out, or_3_out, S1, S2, S3;

  not not_1 (not_1_out, S1);
  not not_2 (not_2_out, S3);
  not not_3 (not_3_out, contains);
  not not_4 (not_4_out, read);
  not not_5 (not_5_out, S1);
  not not_6 (not_6_out, S2);
  not not_7 (not_7_out, S1);
  not not_8 (not_8_out, read);
  not not_9 (not_9_out, S1);
  not not_10 (not_10_out, S3);
  not not_11 (not_11_out, S2);
  not not_12 (not_12_out, S3);
  not not_13 (not_13_out, S2);
  not not_14 (not_14_out, S3);
  not not_15 (not_15_out, S3);
  not not_16 (not_16_out, S3);
  not not_17 (not_17_out, write);
  not not_18 (not_18_out, S1);
  not not_19 (not_19_out, S2);
  not not_20 (not_20_out, S3);
  not not_21 (not_21_out, S2);
  not not_22 (not_22_out, S3);
  not not_23 (not_23_out, S1);
  not not_24 (not_24_out, S2);
  not not_25 (not_25_out, S3);
  not not_26 (not_26_out, S2);
  not not_27 (not_27_out, S3);
  not not_28 (not_28_out, S1);
  not not_29 (not_29_out, S2);
  not not_30 (not_30_out, S3);
  not not_31 (not_31_out, S1);
  not not_32 (not_32_out, S3);
  and and_1 (and_1_out, not_1_out, S2, not_2_out, not_3_out);
  and and_2 (and_2_out, S2, S3, not_4_out, write);
  and and_3 (and_3_out, S1, S3);
  and and_4 (and_4_out, not_5_out, not_6_out, S3);
  and and_5 (and_5_out, not_7_out, S3, not_8_out);
  and and_6 (and_6_out, not_9_out, S2, not_10_out, contains);
  and and_7 (and_7_out, S2, S3, write);
  and and_8 (and_8_out, S1, not_11_out, not_12_out);
  and and_9 (and_9_out, not_13_out, not_14_out);
  and and_10 (and_10_out, not_15_out, dirty);
  and and_11 (and_11_out, not_16_out, contains);
  and and_12 (and_12_out, S2, S3, not_17_out);
  and and_13 (and_13_out, S2, S3, read);
  and and_14 (and_14_out, S1, S2);
  and and_15 (ready, not_18_out, not_19_out, S3);
  and and_16 (setDirty, S1, S2, not_20_out);
  and and_17 (valid, S1, not_21_out, not_22_out);
  and and_18 (UpdateAge, not_23_out, S2, S3);
  and and_19 (memRead, S1, not_24_out, not_25_out);
  and and_20 (memWrite, S1, not_26_out, S3);
  and and_21 (Write_2, S1, S2, not_27_out);
  and and_22 (init, not_28_out, not_29_out, not_30_out);
  and and_23 (saveContain, not_31_out, S2, not_32_out);
  or or_1 (or_1_out, and_1_out, and_2_out, and_3_out);
  or or_2 (or_2_out, and_4_out, and_5_out, and_6_out, and_7_out, and_8_out);
  or or_3 (or_3_out, and_9_out, and_10_out, and_11_out, and_12_out, and_13_out, and_14_out);
  Register #(.width(1)) State (.D(or_1_out), .Q(S1), .clk(CLK));  // open: en, clr
  Register #(.width(1)) State_2 (.D(or_2_out), .Q(S2), .clk(CLK));  // open: en, clr
  Register #(.width(1)) State_3 (.D(or_3_out), .Q(S3), .clk(CLK));  // open: en, clr
endmodule
